// Logisim project control_logic.circ as structural Verilog: 1 circuit, main circuit control_logic
module control_logic (
  input  [31:0] inst,
  input  BrEq,
  input  BrLt,
  output PCSel,
  output RegWEn,
  output [2:0] ImmSel,
  output BrUn,
  output ASel,
  output BSel,
  output [3:0] ALUSel,
  output MemRW,
  output [1:0] WBSel,
  output CSRSel,
  output CSRWen,
  output isLb,
  output isLh,
  output isSb,
  output isSh
);

  wire and_11_out, and_12_out, and_13_out, and_14_out, and_15_out, and_16_out, comparator_1_eq,
       comparator_2_eq, comparator_3_eq, comparator_4_eq, comparator_5_eq, comparator_6_eq, comparator_7_eq,
       comparator_8_eq, comparator_9_eq, comparator_10_eq, comparator_11_eq, comparator_12_eq,
       comparator_15_eq, comparator_16_eq, comparator_17_eq, comparator_18_eq, comparator_19_eq,
       comparator_20_eq, comparator_21_eq, comparator_22_eq, comparator_23_eq, comparator_24_eq,
       comparator_25_eq, comparator_26_eq, comparator_27_eq, comparator_28_eq, comparator_29_eq,
       comparator_30_eq, comparator_31_eq, comparator_32_eq, comparator_33_eq, comparator_34_eq,
       comparator_35_eq, comparator_38_eq, comparator_39_eq, comparator_41_eq, comparator_42_eq,
       comparator_43_eq, comparator_44_eq, comparator_45_eq, comparator_46_eq, comparator_47_eq,
       comparator_48_eq, comparator_49_eq, comparator_50_eq, comparator_51_eq, comparator_52_eq,
       comparator_53_eq, comparator_54_eq, comparator_55_eq, comparator_56_eq, comparator_57_eq, InstB,
       InstU, InstUJ, isIorR, isMul, isMulh, isSra, isSub, not_1_out, not_2_out, not_3_out, or_7_out,
       or_9_out, or_10_out, WBSelALU, WBSelImm, WBSelPC4;
  wire [1:0] multiplexer_1_out, multiplexer_2_out;
  wire [2:0] multiplexer_10_out, multiplexer_11_out, multiplexer_12_out, multiplexer_13_out;
  wire [3:0] multiplexer_4_out, multiplexer_5_out, multiplexer_6_out, multiplexer_7_out, multiplexer_8_out;

  Comparator #(.width(7)) comparator_1 (.a(inst[6:0]), .b(7'b0000011), .eq(comparator_1_eq));  // open: gt, lt
  Comparator #(.width(7)) comparator_2 (.a(inst[6:0]), .b(7'b0010011), .eq(comparator_2_eq));  // open: gt, lt
  Comparator #(.width(7)) comparator_3 (.a(inst[6:0]), .b(7'b1100011), .eq(comparator_3_eq));  // open: gt, lt
  Comparator #(.width(7)) comparator_4 (.a(inst[6:0]), .b(7'b0010111), .eq(comparator_4_eq));  // open: gt, lt
  Comparator #(.width(7)) comparator_5 (.a(inst[6:0]), .b(7'b0110111), .eq(comparator_5_eq));  // open: gt, lt
  Comparator #(.width(7)) comparator_6 (.a(inst[6:0]), .b(7'b1101111), .eq(comparator_6_eq));  // open: gt, lt
  Comparator #(.width(7)) comparator_7 (.a(inst[6:0]), .b(7'b1100111), .eq(comparator_7_eq));  // open: gt, lt
  Multiplexer #(.enable("false"), .width(2)) multiplexer_1 (
    .in0(2'b00), .in1(2'b01), .out(multiplexer_1_out), .sel(WBSelALU));
  Comparator #(.width(7)) comparator_8 (.a(inst[6:0]), .b(7'b0010011), .eq(comparator_8_eq));  // open: gt, lt
  Comparator #(.width(7)) comparator_9 (.a(inst[6:0]), .b(7'b0010111), .eq(comparator_9_eq));  // open: gt, lt
  Comparator #(.width(7)) comparator_10 (.a(inst[6:0]), .b(7'b0110011), .eq(comparator_10_eq));  // open: gt, lt
  Comparator #(.width(7)) comparator_11 (.a(inst[6:0]), .b(7'b1100111), .eq(comparator_11_eq));  // open: gt, lt
  Comparator #(.width(7)) comparator_12 (.a(inst[6:0]), .b(7'b1101111), .eq(comparator_12_eq));  // open: gt, lt
  Comparator #(.width(7)) comparator_13 (.a(inst[6:0]), .b(7'b0110111), .eq(WBSelImm));  // open: gt, lt
  or or_1 (BSel, comparator_1_eq, comparator_2_eq, comparator_3_eq, comparator_4_eq, comparator_5_eq, comparator_6_eq, comparator_7_eq);
  Comparator #(.width(7)) comparator_14 (.a(inst[6:0]), .b(7'b1110011), .eq(CSRWen));  // open: gt, lt
  Multiplexer #(.enable("false"), .width(2)) multiplexer_2 (
    .in0(multiplexer_1_out), .in1(2'b10), .out(multiplexer_2_out), .sel(WBSelPC4));
  or or_2 (WBSelALU, comparator_8_eq, comparator_9_eq, comparator_10_eq);
  or or_3 (WBSelPC4, comparator_11_eq, comparator_12_eq);
  Multiplexer #(.enable("false"), .width(2)) multiplexer_3 (
    .in0(multiplexer_2_out), .in1(2'b11), .out(WBSel), .sel(WBSelImm));
  Comparator #(.width(7)) comparator_15 (.a(inst[31:25]), .b(7'b0100000), .eq(comparator_15_eq));  // open: gt, lt
  Comparator #(.width(3)) comparator_16 (.a(inst[14:12]), .b(3'b000), .eq(comparator_16_eq));  // open: gt, lt
  Comparator #(.width(7)) comparator_17 (.a(inst[6:0]), .b(7'b0110011), .eq(comparator_17_eq));  // open: gt, lt
  Multiplexer #(.enable("false"), .select(3), .width(4)) multiplexer_4 (
    .in0(4'b0000), .in1(4'b0110), .in2(4'b0111), .in3(4'b1011), .in4(4'b0011), .in5(4'b0100), .in6(4'b0010),
    .in7(4'b0001), .out(multiplexer_4_out), .sel(inst[14:12]));
  and and_1 (isSub, comparator_15_eq, comparator_16_eq, comparator_17_eq);
  Comparator #(.width(7)) comparator_18 (.a(inst[6:0]), .b(7'b0110011), .eq(comparator_18_eq));  // open: gt, lt
  Comparator #(.width(7)) comparator_19 (.a(inst[6:0]), .b(7'b0000011), .eq(comparator_19_eq));  // open: gt, lt
  Comparator #(.width(7)) comparator_20 (.a(inst[6:0]), .b(7'b0010011), .eq(comparator_20_eq));  // open: gt, lt
  Comparator #(.width(7)) comparator_21 (.a(inst[6:0]), .b(7'b1101111), .eq(comparator_21_eq));  // open: gt, lt
  Comparator #(.width(7)) comparator_22 (.a(inst[6:0]), .b(7'b0110111), .eq(comparator_22_eq));  // open: gt, lt
  Comparator #(.width(7)) comparator_23 (.a(inst[6:0]), .b(7'b0010111), .eq(comparator_23_eq));  // open: gt, lt
  Comparator #(.width(7)) comparator_24 (.a(inst[6:0]), .b(7'b1100111), .eq(comparator_24_eq));  // open: gt, lt
  Comparator #(.width(7)) comparator_25 (.a(inst[6:0]), .b(7'b0010111), .eq(comparator_25_eq));  // open: gt, lt
  Multiplexer #(.enable("false"), .width(4)) multiplexer_5 (
    .in0(multiplexer_4_out), .in1(4'b1100), .out(multiplexer_5_out), .sel(isSub));
  Multiplexer #(.enable("false"), .width(4)) multiplexer_6 (
    .in0(multiplexer_5_out), .in1(4'b1010), .out(multiplexer_6_out), .sel(isMul));
  or or_4 (RegWEn, comparator_18_eq, comparator_19_eq, comparator_20_eq, comparator_21_eq, comparator_22_eq, comparator_23_eq, comparator_24_eq);
  or or_5 (ASel, InstB, InstUJ, comparator_25_eq);
  Comparator #(.width(7)) comparator_26 (.a(inst[31:25]), .b(7'b0000001), .eq(comparator_26_eq));  // open: gt, lt
  Comparator #(.width(3)) comparator_27 (.a(inst[14:12]), .b(3'b000), .eq(comparator_27_eq));  // open: gt, lt
  Comparator #(.width(7)) comparator_28 (.a(inst[6:0]), .b(7'b0110011), .eq(comparator_28_eq));  // open: gt, lt
  Comparator #(.width(7)) comparator_29 (.a(inst[6:0]), .b(7'b0000011), .eq(comparator_29_eq));  // open: gt, lt
  Comparator #(.width(7)) comparator_30 (.a(inst[6:0]), .b(7'b0100011), .eq(comparator_30_eq));  // open: gt, lt
  Comparator #(.width(3)) comparator_31 (.a(inst[14:12]), .b(3'b000), .eq(comparator_31_eq));  // open: gt, lt
  Comparator #(.width(3)) comparator_32 (.a(inst[14:12]), .b(3'b001), .eq(comparator_32_eq));  // open: gt, lt
  Multiplexer #(.enable("false"), .width(4)) multiplexer_7 (
    .in0(multiplexer_6_out), .in1(4'b1110), .out(multiplexer_7_out), .sel(isMulh));
  and and_2 (isMul, comparator_26_eq, comparator_27_eq, comparator_28_eq);
  and and_3 (isLb, comparator_29_eq, comparator_31_eq);
  and and_4 (isLh, comparator_29_eq, comparator_32_eq);
  and and_5 (isSb, comparator_30_eq, comparator_31_eq);
  and and_6 (isSh, comparator_30_eq, comparator_32_eq);
  Multiplexer #(.enable("false"), .width(4)) multiplexer_8 (
    .in0(multiplexer_7_out), .in1(4'b0101), .out(multiplexer_8_out), .sel(isSra));
  Multiplexer #(.enable("false"), .width(4)) multiplexer_9 (
    .in0(4'b0000), .in1(multiplexer_8_out), .out(ALUSel), .sel(isIorR));
  Comparator #(.width(7)) comparator_33 (.a(inst[31:25]), .b(7'b0000001), .eq(comparator_33_eq));  // open: gt, lt
  Comparator #(.width(3)) comparator_34 (.a(inst[14:12]), .b(3'b001), .eq(comparator_34_eq));  // open: gt, lt
  Comparator #(.width(7)) comparator_35 (.a(inst[6:0]), .b(7'b0110011), .eq(comparator_35_eq));  // open: gt, lt
  Multiplexer #(.enable("false"), .width(3)) multiplexer_10 (
    .in0(3'b000), .in1(3'b001), .out(multiplexer_10_out), .sel(MemRW));
  and and_7 (isMulh, comparator_33_eq, comparator_34_eq, comparator_35_eq);
  Multiplexer #(.enable("false"), .width(3)) multiplexer_11 (
    .in0(multiplexer_10_out), .in1(3'b010), .out(multiplexer_11_out), .sel(InstB));
  Comparator #(.width(7)) comparator_36 (.a(inst[6:0]), .b(7'b0100011), .eq(MemRW));  // open: gt, lt
  Comparator #(.width(7)) comparator_37 (.a(inst[6:0]), .b(7'b1100011), .eq(InstB));  // open: gt, lt
  Comparator #(.width(7)) comparator_38 (.a(inst[6:0]), .b(7'b0010111), .eq(comparator_38_eq));  // open: gt, lt
  Comparator #(.width(7)) comparator_39 (.a(inst[6:0]), .b(7'b0110111), .eq(comparator_39_eq));  // open: gt, lt
  Comparator #(.width(7)) comparator_40 (.a(inst[6:0]), .b(7'b1101111), .eq(InstUJ));  // open: gt, lt
  Comparator #(.width(7)) comparator_41 (.a(inst[6:0]), .b(7'b1110011), .eq(comparator_41_eq));  // open: gt, lt
  Comparator #(.width(3)) comparator_42 (.a(inst[14:12]), .b(3'b101), .eq(comparator_42_eq));  // open: gt, lt
  Comparator #(.width(3)) comparator_43 (.a(inst[14:12]), .b(3'b110), .eq(comparator_43_eq));  // open: gt, lt
  Comparator #(.width(3)) comparator_44 (.a(inst[14:12]), .b(3'b111), .eq(comparator_44_eq));  // open: gt, lt
  or or_6 (InstU, comparator_38_eq, comparator_39_eq);
  and and_8 (CSRSel, comparator_41_eq, comparator_42_eq);
  Multiplexer #(.enable("false"), .width(3)) multiplexer_12 (
    .in0(multiplexer_11_out), .in1(3'b011), .out(multiplexer_12_out), .sel(InstU));
  Comparator #(.width(7)) comparator_45 (.a(inst[6:0]), .b(7'b0110011), .eq(comparator_45_eq));  // open: gt, lt
  Comparator #(.width(7)) comparator_46 (.a(inst[6:0]), .b(7'b0010011), .eq(comparator_46_eq));  // open: gt, lt
  Comparator #(.width(7)) comparator_47 (.a(inst[31:25]), .b(7'b0100000), .eq(comparator_47_eq));  // open: gt, lt
  Comparator #(.width(3)) comparator_48 (.a(inst[14:12]), .b(3'b101), .eq(comparator_48_eq));  // open: gt, lt
  Comparator #(.width(7)) comparator_49 (.a(inst[6:0]), .b(7'b0110011), .eq(comparator_49_eq));  // open: gt, lt
  Multiplexer #(.enable("false"), .width(3)) multiplexer_13 (
    .in0(multiplexer_12_out), .in1(3'b100), .out(multiplexer_13_out), .sel(InstUJ));
  or or_7 (or_7_out, comparator_43_eq, comparator_44_eq);
  Comparator #(.width(3)) comparator_50 (.a(inst[14:12]), .b(3'b000), .eq(comparator_50_eq));  // open: gt, lt
  Comparator #(.width(3)) comparator_51 (.a(inst[14:12]), .b(3'b001), .eq(comparator_51_eq));  // open: gt, lt
  Comparator #(.width(3)) comparator_52 (.a(inst[14:12]), .b(3'b100), .eq(comparator_52_eq));  // open: gt, lt
  Comparator #(.width(3)) comparator_53 (.a(inst[14:12]), .b(3'b101), .eq(comparator_53_eq));  // open: gt, lt
  Comparator #(.width(3)) comparator_54 (.a(inst[14:12]), .b(3'b110), .eq(comparator_54_eq));  // open: gt, lt
  Comparator #(.width(3)) comparator_55 (.a(inst[14:12]), .b(3'b111), .eq(comparator_55_eq));  // open: gt, lt
  and and_9 (isSra, comparator_47_eq, comparator_48_eq, comparator_49_eq);
  Multiplexer #(.enable("false"), .width(3)) multiplexer_14 (
    .in0(multiplexer_13_out), .in1(3'b101), .out(ImmSel), .sel(CSRSel));
  and and_10 (BrUn, InstB, or_7_out);
  not not_1 (not_1_out, BrEq);
  not not_2 (not_2_out, BrLt);
  not not_3 (not_3_out, BrLt);
  or or_8 (isIorR, comparator_45_eq, comparator_46_eq);
  and and_11 (and_11_out, InstB, comparator_50_eq, BrEq);
  and and_12 (and_12_out, InstB, comparator_51_eq, not_1_out);
  and and_13 (and_13_out, InstB, comparator_52_eq, BrLt);
  and and_14 (and_14_out, InstB, comparator_53_eq, not_2_out);
  and and_15 (and_15_out, InstB, comparator_54_eq, BrLt);
  and and_16 (and_16_out, InstB, comparator_55_eq, not_3_out);
  Comparator #(.width(7)) comparator_56 (.a(inst[6:0]), .b(7'b1100111), .eq(comparator_56_eq));  // open: gt, lt
  Comparator #(.width(7)) comparator_57 (.a(inst[6:0]), .b(7'b1101111), .eq(comparator_57_eq));  // open: gt, lt
  or or_9 (or_9_out, and_11_out, and_12_out, and_13_out, and_14_out, and_15_out, and_16_out);
  or or_10 (or_10_out, comparator_56_eq, comparator_57_eq);
  or or_11 (PCSel, or_9_out, or_10_out);

  // Other names for the same wires on the sheet: opcode[6:0] = inst[6:0]; rd[4:0] = inst[11:7];
  //   funct3[2:0] = inst[14:12]; rs1[4:0] = inst[19:15]; rs2[4:0] = inst[24:20]; funct7[6:0] = inst[31:25];
  //   InstCSR = CSRSel; InstS = MemRW

  // Notes on the sheet:
  //   INPUTS to your circuit
  //   Decode
  //   WBSel
  //   BSel
  //   DON'T CHANGE THE LOCATIONS OF THE INPUTS AND OUTPUTS!
  //   OUTPUT from your circuit
  //   Write Enable
  //   ASel
  //   Write mask
  //   ALU SEL
  //   Imm select
  //   PCSel
endmodule
