// Logisim project cpu.circ as structural Verilog: 1 circuit, main circuit cpu
module cpu (
  input  clk,
  input  [31:0] INSTRUCTION,
  input  [31:0] READ_DATA,
  output [31:0] WRITE_ADDRESS,
  output [31:0] PROGRAM_COUNTER,
  output [31:0] ra,
  output [31:0] sp,
  output [31:0] t0,
  output [31:0] t1,
  output [31:0] t2,
  output [31:0] s0,
  output [31:0] s1,
  output [31:0] a0,
  output [31:0] tohost,
  output [3:0] WRITE_ENABLE,
  output [31:0] WRITE_DATA
);

  wire ASel, BrEq, BrLt, BrUn, BSel, CSRSel, CSRWen, isLb, isLh, isSb, isSh, MemRW, PCSel, RegWEn;
  wire [1:0] WBSel;
  wire [2:0] funct3, ImmSel;
  wire [3:0] ALUSel, multiplexer_8_out, multiplexer_9_out;
  wire [6:0] funct7;
  wire [24:0] INSTRUCTION_t;
  wire [31:0] adder_1_out, adder_2_out, bit_extender_1_out, bit_extender_2_out, data1, FIXED_DATA, imm,
       multiplexer_1_out, multiplexer_2_out, multiplexer_3_out, multiplexer_4_out, multiplexer_5_out,
       multiplexer_6_out, PROGRAM_COUNTER_t, WB_DATA;

  Adder #(.width(32)) adder_1 (.a(PROGRAM_COUNTER), .b(32'h4), .out(adder_1_out));  // open: cin, cout
  Multiplexer #(.enable("false"), .width(32)) multiplexer_1 (
    .in0(adder_1_out), .in1(WRITE_ADDRESS), .out(multiplexer_1_out), .sel(PCSel));
  Multiplexer #(.enable("false"), .width(32)) multiplexer_2 (
    .in0(INSTRUCTION), .in1(32'h13), .out(multiplexer_2_out), .sel(PCSel));
  Register #(.width(32)) PC (.D(multiplexer_1_out), .clk(clk), .Q(PROGRAM_COUNTER));  // open: en, clr
  Register #(.width(32)) register_1 (.D(PROGRAM_COUNTER), .clk(clk), .Q(PROGRAM_COUNTER_t));  // open: en, clr
  Register #(.width(32)) register_2 (
    .D(multiplexer_2_out), .clk(clk), .Q({funct7, INSTRUCTION_t[24:15], funct3, INSTRUCTION_t[11:0]}));  // open: en, clr
  // imm_gen imm_gen_1: pin names not known; wires that end beside it: {funct7, INSTRUCTION_t[24:15], funct3, INSTRUCTION_t[11:0]}, ImmSel, imm
  control_logic control_logic_1 (
    .CSRWen(CSRWen), .isLb(isLb), .isLh(isLh), .isSb(isSb), .isSh(isSh), .PCSel(PCSel), .RegWEn(RegWEn),
    .ImmSel(ImmSel), .BrUn(BrUn), .ASel(ASel), .BSel(BSel), .ALUSel(ALUSel), .MemRW(MemRW), .WBSel(WBSel),
    .CSRSel(CSRSel), .inst({funct7, INSTRUCTION_t[24:15], funct3, INSTRUCTION_t[11:0]}), .BrEq(BrEq),
    .BrLt(BrLt));
  // branch_comp branch_comp_1: pin names not known; wires that end beside it: data1, WRITE_DATA, BrUn, BrEq, BrLt
  regfile regfile_1 (
    .rs1(INSTRUCTION_t[19:15]), .rs2(INSTRUCTION_t[24:20]), .rd(INSTRUCTION_t[11:7]), .Write_Data(WB_DATA),
    .RegWEn(RegWEn), .clk(clk), .ra(ra), .sp(sp), .t0(t0), .t1(t1), .t2(t2), .s0(s0), .s1(s1), .a0(a0),
    .Read_Data_1(data1), .Read_Data_2(WRITE_DATA));
  Multiplexer #(.enable("false"), .width(32)) multiplexer_3 (
    .in0(data1), .in1(imm), .out(multiplexer_3_out), .sel(CSRSel));
  csr csr_1 (.CSR_address(12'h51e), .CSR_din(multiplexer_3_out), .CSR_WE(CSRWen), .clk(clk), .tohost(tohost));
  Multiplexer #(.enable("false"), .width(32)) multiplexer_4 (
    .in0(data1), .in1(PROGRAM_COUNTER_t), .out(multiplexer_4_out), .sel(ASel));
  Multiplexer #(.enable("false"), .width(32)) multiplexer_5 (
    .in0(WRITE_DATA), .in1(imm), .out(multiplexer_5_out), .sel(BSel));
  alu alu_1 (.Result(WRITE_ADDRESS), .A(multiplexer_4_out), .B(multiplexer_5_out), .ALUSel(ALUSel));
  assign bit_extender_1_out = {{16{READ_DATA[15]}}, READ_DATA[15:0]};  // Bit_Extender bit_extender_1
  assign bit_extender_2_out = {{24{READ_DATA[7]}}, READ_DATA[7:0]};  // Bit_Extender bit_extender_2
  Multiplexer #(.enable("false"), .width(32)) multiplexer_6 (
    .in0(READ_DATA), .in1(bit_extender_1_out), .out(multiplexer_6_out), .sel(isLh));
  Multiplexer #(.enable("false"), .width(32)) multiplexer_7 (
    .in0(multiplexer_6_out), .in1(bit_extender_2_out), .out(FIXED_DATA), .sel(isLb));
  Multiplexer #(.enable("false"), .width(4)) multiplexer_8 (
    .in0(4'b1111), .in1(4'b0011), .out(multiplexer_8_out), .sel(isSh));
  Multiplexer #(.enable("false"), .width(4)) multiplexer_9 (
    .in0(multiplexer_8_out), .in1(4'b0001), .out(multiplexer_9_out), .sel(isSb));
  Multiplexer #(.enable("false"), .width(4)) multiplexer_10 (
    .in0(4'b0000), .in1(multiplexer_9_out), .out(WRITE_ENABLE), .sel(MemRW));
  Adder #(.width(32)) adder_2 (.a(PROGRAM_COUNTER_t), .b(32'h4), .out(adder_2_out));  // open: cin, cout
  Multiplexer #(.enable("false"), .select(2), .width(32)) multiplexer_11 (
    .in0(FIXED_DATA), .in1(WRITE_ADDRESS), .in2(adder_2_out), .in3(imm), .out(WB_DATA), .sel(WBSel));

  // Other names for the same wires on the sheet: ALU_OUT[31:0] = WRITE_ADDRESS; data2[31:0] = WRITE_DATA;
  //   IN_temporary[31:0] = INSTRUCTION; op[6:0] = INSTRUCTION_t[6:0]; rd[4:0] = INSTRUCTION_t[11:7];
  //   INSTRUCTION_t (some bits) = {funct7, funct3}; rs1[4:0] = INSTRUCTION_t[19:15]; rs2[4:0] = INSTRUCTION_t[24:20];
  //   PC_temporary[31:0] = PROGRAM_COUNTER

  // Notes on the sheet:
  //   Output to IMEM
  //   IMEM (do **NOT** move this)
  //   Inputs from IMEM
  //   It is OK to move the PC, RegFile, ALU, MEM, Branch Comp, Imm Gen, and Control Logic to wherever is most convenient for you when constructing your CPU, and to delete this text
  //   Inputs/Outputs for testing. Do **NOT** move these.
  //   Outputs To DMEM
  //   DMEM (do **NOT** move this)
  //   Inputs From DMEM
endmodule
